# Fritzing sketch MiniD1ESP32 (saved by Fritzing 0.9.3b)
breadboards: 1

parts:
  A1 = MH-ET Live Minikit for ESP32
  Componente2 = FTDI Basic Programmer
  S3 = Pushbutton [package="[THT]"]
  S4 = Pushbutton [package="[THT]"]
  R10 = Resistor [tolerance=±5% resistance=68 package="0402 [SMD]"]
  R11 = Resistor [tolerance=±5% resistance=68 package="0402 [SMD]"]
  R12 = Resistor [tolerance=±5% resistance=22 package="0402 [SMD]"]
  R13 = Resistor [tolerance=±5% resistance=220 package="0402 [SMD]"]
  R14 = Resistor [tolerance=±5% resistance=22 package="0402 [SMD]"]
  R15 = Resistor [tolerance=±5% resistance=220 package="0402 [SMD]"]
  R16 = Resistor [tolerance=±5% resistance=220 package="0402 [SMD]"]
  R17 = Resistor [tolerance=±5% resistance=1k package="0402 [SMD]"]
  R18 = Resistor [tolerance=±5% resistance=1k package="0402 [SMD]"]
  LED10 = RGB LED (com. cathode, rgb) [package="5 mm [THT]"]
  LED11 = RGB LED (com. cathode, rgb) [package="5 mm [THT]"]
  LED12 = LED - 3mm [color="Yellow (592nm)" package="3 mm [THT]"]

nets:
  N1: A1.GND, S4.Pin_1, S4.Pin_2, LED10.common_cathode, LED11.common_cathode, LED12.cathode
  N2: A1.IO18, S4.Pin_3, S4.Pin_4, R18.Pin_0
  N3: A1.IO19, R13.Pin_1
  N4: A1.IO23, R10.Pin_1
  N5: A1.IO5, S3.Pin_3, S3.Pin_4, R17.Pin_0
  N6: A1.IO17, Componente2.RXI
  N7: A1.IO16, Componente2.TXO
  N8: A1.IO27, R12.Pin_1
  N9: A1.IO25, R11.Pin_1
  N10: A1.TDI, R16.Pin_1
  N11: A1.IO4, R15.Pin_1
  N12: A1.IO2, R14.Pin_1
  N13: S3.Pin_1, S3.Pin_2, R17.Pin_1, R18.Pin_1
  N14: R10.Pin_0, LED11.red_anode
  N15: R11.Pin_0, LED10.red_anode
  N16: R12.Pin_0, LED11.blue_anode
  N17: R13.Pin_0, LED12.anode
  N18: R14.Pin_0, LED10.blue_anode
  N19: R15.Pin_0, LED10.green_anode
  N20: R16.Pin_0, LED11.green_anode

notes:
  React
  Mode
  Manual
  Pulse
  Status
  Pulse

custom parts:
  MH-ET Live Minikit for ESP32: MH-ET Live Minikit for ESP32 ( http://mh.nodebb.com/topic/8/mh-et-live-minikit-for-esp32/2/) PCB footprint is invalid.
