# Fritzing sketch wemosD1R32 (saved by Fritzing 0.9.3b)
breadboards: 1

parts:
  WeMos_D1_R1 = WeMos D1 R2
  Componente1 = FTDI Basic Programmer
  S1 = Pushbutton [package="[THT]"]
  S2 = Pushbutton [package="[THT]"]
  R1 = Resistor [tolerance=±5% resistance=1k package="0402 [SMD]"]
  R2 = Resistor [tolerance=±5% resistance=1k package="0402 [SMD]"]
  R3 = Resistor [tolerance=±5% resistance=220 package="0402 [SMD]"]
  R4 = Resistor [tolerance=±5% resistance=220 package="0402 [SMD]"]
  R5 = Resistor [tolerance=±5% resistance=68 package="0402 [SMD]"]
  R6 = Resistor [tolerance=±5% resistance=68 package="0402 [SMD]"]
  LED7 = RGB LED (com. cathode, rgb) [package="5 mm [THT]"]
  R7 = Resistor [tolerance=±5% resistance=22 package="0402 [SMD]"]
  LED8 = RGB LED (com. cathode, rgb) [package="5 mm [THT]"]
  R8 = Resistor [tolerance=±5% resistance=22 package="0402 [SMD]"]
  LED9 = LED - 3mm [color="Yellow (592nm)" package="3 mm [THT]"]
  R9 = Resistor [tolerance=±5% resistance=220 package="0402 [SMD]"]

nets:
  N1: WeMos_D1_R1.D3, R7.Pin_1
  N2: WeMos_D1_R1.D4, Componente1.RXI
  N3: WeMos_D1_R1.(D5), Componente1.TXO
  N4: WeMos_D1_R1.(D6), R8.Pin_1
  N5: WeMos_D1_R1.D8, R3.Pin_1
  N6: WeMos_D1_R1.D10, S1.Pin_3, S1.Pin_4, R2.Pin_0
  N7: WeMos_D1_R1.D11, R6.Pin_1
  N8: WeMos_D1_R1.D12, R9.Pin_1
  N9: WeMos_D1_R1.D13, S2.Pin_3, S2.Pin_4, R1.Pin_0
  N10: WeMos_D1_R1.GND, S2.Pin_1, S2.Pin_2, LED7.common_cathode, LED8.common_cathode, LED9.cathode
  N11: WeMos_D1_R1.A0, R5.Pin_1
  N12: WeMos_D1_R1.3.3V, S1.Pin_1, S1.Pin_2, R1.Pin_1, R2.Pin_1
  N13: R3.Pin_0, LED8.green_anode
  N14: R4.Pin_0, LED7.green_anode
  N15: R5.Pin_0, LED7.red_anode
  N16: R6.Pin_0, LED8.red_anode
  N17: LED7.blue_anode, R7.Pin_0
  N18: LED8.blue_anode, R8.Pin_0
  N19: LED9.anode, R9.Pin_0

notes:
  Pulse
  Mode
  Status
  Manual
  Pulse
  React

custom parts:
  WeMos D1 R2: The D1 R2 is a mini wifi board based on the ESP-8266EX.
